# Fritzing sketch IR (saved by Fritzing 1.0.6)
perfboards: 1

parts:
  J1 = Header 12 [package=1x12_machine-pin-header_lock.004]
  IR1 = tl1838 [package=THT]
  R1 = Resistor [tolerance=±5% power=0.25W resistance=22 package=THT]
  LED1 = LED - 5mm [color="Infrared (940nm)" current=30mA package="5 mm [THT]"]
  R2 = Resistor [tolerance=±5% power=0.25W resistance=470 package=THT]
  Q1 = NPN-Transistor [mpn=2N2222 package="TO92 [THT]"]

nets:
  N1: J1.1, Q1.E
  N2: J1.2, R1.Pin_1
  N3: J1.7, R2.Pin_0
  N4: J1.8, IR1.OUT
  N5: J1.11, IR1.VCC
  N6: J1.12, IR1.GND
  N7: R1.Pin_0, LED1.anode
  N8: LED1.cathode, Q1.C
  N9: R2.Pin_1, Q1.B

custom parts:
  tl1838: The TL1838 is a miniaturized receiver for infrared remote control systems. A PIN diode and a preamplifier are assembled on a lead frame, the epoxy package acts as an IR filter. The demodulated output signal can be directly decoded by a microprocessor.
