# Fritzing sketch sx_lora (saved by Fritzing 1.0.6)
perfboards: 1

parts:
  JP2 = Header 12 [package=1x12_machine-pin-header_lock.004]
  J3 = E2200-900T30
  J2 = double row male pin header, 6 pins [form="♂ (male)"]
  J1 = double row male pin header, 6 pins [form="♂ (male)"]
  C2 = Ceramic Capacitor [capacitance=0.47mF voltage=35V package="100 mil [THT, multilayer]"]

nets:
  N1: JP2.1, J3.M0, J1.pin1, C2.0
  N2: JP2.2, J2.pin1, C2.1
  N3: JP2.3, J2.pin4
  N4: JP2.4, J3.AUX, J1.pin5
  N5: JP2.5, J3.M1, J1.pin2
  N6: JP2.6, J3.TXD, J1.pin4
  N7: JP2.7, J2.pin3
  N8: JP2.8, J3.RXD, J1.pin3
  N9: JP2.9, J2.pin2
  N10: JP2.10, J2.pin6
  N11: J3.VCC, J2.pin5, J1.pin6

custom parts:
  E2200-900T30: Ebyte E220-900T30D LoRa Modul
